// Logisim project Архитектура Практика.circ as structural Verilog: 40 circuits, main circuit ALU
module ALU (
  input  [7:0] in_1,
  input  [1:0] in_2,
  input  [7:0] in_3,
  output [7:0] out_4
);

  wire [7:0] adder_1_out, demultiplexer_1_out0, demultiplexer_1_out1, demultiplexer_1_out2,
       demultiplexer_1_out3, demultiplexer_2_out0, demultiplexer_2_out1, demultiplexer_2_out2,
       demultiplexer_2_out3, divider_1_out, multiplier_1_out, subtractor_1_out;

  Demultiplexer #(.select(2), .width(8), .enable("false")) demultiplexer_1 (
    .out0(demultiplexer_1_out0), .out1(demultiplexer_1_out1), .out2(demultiplexer_1_out2),
    .out3(demultiplexer_1_out3), .in(in_1), .sel(in_2));
  Demultiplexer #(.select(2), .width(8), .enable("false")) demultiplexer_2 (
    .out0(demultiplexer_2_out0), .out1(demultiplexer_2_out1), .out2(demultiplexer_2_out2),
    .out3(demultiplexer_2_out3), .in(in_3), .sel(in_2));
  Multiplexer #(.select(2), .width(8), .enable("false")) multiplexer_1 (
    .in0(adder_1_out), .in1(subtractor_1_out), .in2(multiplier_1_out), .in3(divider_1_out), .out(out_4),
    .sel(in_2));
  Adder_part adder_1 (.a(demultiplexer_1_out0), .b(demultiplexer_2_out0), .out(adder_1_out));  // open: cin, cout
  Subtractor subtractor_1 (
    .a(demultiplexer_1_out1), .b(demultiplexer_2_out1), .out(subtractor_1_out));  // open: bin, bout
  Multiplier multiplier_1 (
    .a(demultiplexer_1_out2), .b(demultiplexer_2_out2), .out(multiplier_1_out));  // open: cin, cout
  Divider divider_1 (.a(demultiplexer_1_out3), .b(demultiplexer_2_out3), .out(divider_1_out));  // open: upper, rem
endmodule

module OR_8_bit (
  input  [7:0] in_1,
  input  [7:0] in_2,
  output [7:0] out_3
);

  assign out_3 = in_1 | in_2;  // OR_Gate or_1, 8 bits wide
endmodule

module AND_8_bit (
  input  [7:0] in_1,
  input  [7:0] in_2,
  output [7:0] out_3
);

  assign out_3 = in_1 & in_2;  // AND_Gate and_1, 8 bits wide
endmodule

module NOT_8_bit (
  input  [7:0] in_1,
  output [7:0] out_2
);

  assign out_2 = ~in_1;  // NOT_Gate not_1, 8 bits wide
endmodule

module XOR_8_bit (
  input  [7:0] in_1,
  input  [7:0] in_2,
  output [7:0] out_3
);

  assign out_3 = in_1 ^ in_2;  // XOR_Gate xor_1, 8 bits wide
endmodule

module LOGIC_OR (
  input  [7:0] in_1,
  input  [7:0] in_2,
  output out_3
);

  wire or_1_out, or_2_out;

  or or_1 (or_1_out, in_1[0], in_1[1], in_1[2], in_1[3], in_1[4], in_1[5], in_1[6], in_1[7]);
  or or_2 (or_2_out, in_2[0], in_2[1], in_2[2], in_2[3], in_2[4], in_2[5], in_2[6], in_2[7]);
  or or_3 (out_3, or_1_out, or_2_out);
endmodule

module LOGIC_AND (
  input  [7:0] in_1,
  input  [7:0] in_2,
  output out_3
);

  wire or_1_out, or_2_out;

  or or_1 (or_1_out, in_1[0], in_1[1], in_1[2], in_1[3], in_1[4], in_1[5], in_1[6], in_1[7]);
  or or_2 (or_2_out, in_2[0], in_2[1], in_2[2], in_2[3], in_2[4], in_2[5], in_2[6], in_2[7]);
  and and_1 (out_3, or_1_out, or_2_out);
endmodule

module LOGIC_NOT (
  input  [7:0] in_1,
  output out_2
);

  wire or_1_out;

  or or_1 (or_1_out, in_1[0], in_1[1], in_1[2], in_1[3], in_1[4], in_1[5], in_1[6], in_1[7]);
  not not_1 (out_2, or_1_out);
endmodule

module LOGIC_XOR (
  input  [7:0] in_1,
  input  [7:0] in_2,
  output out_3
);

  wire or_1_out, or_2_out;

  or or_1 (or_1_out, in_1[0], in_1[1], in_1[2], in_1[3], in_1[4], in_1[5], in_1[6], in_1[7]);
  or or_2 (or_2_out, in_2[0], in_2[1], in_2[2], in_2[3], in_2[4], in_2[5], in_2[6], in_2[7]);
  xor xor_1 (out_3, or_1_out, or_2_out);
endmodule

module L_A_Shift_Left (
  input  [7:0] in_1,
  input  [2:0] in_2,
  output [7:0] out_3,
  output out_4
);

  wire multiplexer_1_out, multiplexer_2_out, multiplexer_3_out, multiplexer_4_out, multiplexer_5_out,
       multiplexer_6_out, multiplexer_7_out, multiplexer_8_out, multiplexer_9_out, multiplexer_10_out,
       multiplexer_11_out, multiplexer_12_out, multiplexer_13_out, multiplexer_14_out, multiplexer_15_out,
       multiplexer_16_out;
  wire [2:0] not_1_out;
  wire [3:0] bitadder_1_out, bitadder_2_out;

  Multiplexer #(.enable("false")) multiplexer_1 (
    .in0(1'b0), .in1(in_1[0]), .out(multiplexer_1_out), .sel(not_1_out[0]));
  Multiplexer #(.enable("false")) multiplexer_2 (
    .in0(in_1[0]), .in1(in_1[1]), .out(multiplexer_2_out), .sel(not_1_out[0]));
  Multiplexer #(.enable("false")) multiplexer_3 (
    .in0(in_1[1]), .in1(in_1[2]), .out(multiplexer_3_out), .sel(not_1_out[0]));
  Multiplexer #(.enable("false")) multiplexer_4 (
    .in0(in_1[2]), .in1(in_1[3]), .out(multiplexer_4_out), .sel(not_1_out[0]));
  Multiplexer #(.enable("false")) multiplexer_5 (
    .in0(in_1[3]), .in1(in_1[4]), .out(multiplexer_5_out), .sel(not_1_out[0]));
  Multiplexer #(.enable("false")) multiplexer_6 (
    .in0(in_1[4]), .in1(in_1[5]), .out(multiplexer_6_out), .sel(not_1_out[0]));
  Multiplexer #(.enable("false")) multiplexer_7 (
    .in0(in_1[5]), .in1(in_1[6]), .out(multiplexer_7_out), .sel(not_1_out[0]));
  Multiplexer #(.enable("false")) multiplexer_8 (
    .in0(in_1[6]), .in1(in_1[7]), .out(multiplexer_8_out), .sel(not_1_out[0]));
  assign not_1_out = ~in_2;  // NOT_Gate not_1, 3 bits wide
  Multiplexer #(.enable("false")) multiplexer_9 (
    .in0(1'b0), .in1(multiplexer_1_out), .out(multiplexer_9_out), .sel(not_1_out[1]));
  Multiplexer #(.enable("false")) multiplexer_10 (
    .in0(1'b0), .in1(multiplexer_2_out), .out(multiplexer_10_out), .sel(not_1_out[1]));
  Multiplexer #(.enable("false")) multiplexer_11 (
    .in0(multiplexer_1_out), .in1(multiplexer_3_out), .out(multiplexer_11_out), .sel(not_1_out[1]));
  Multiplexer #(.enable("false")) multiplexer_12 (
    .in0(multiplexer_2_out), .in1(multiplexer_4_out), .out(multiplexer_12_out), .sel(not_1_out[1]));
  Multiplexer #(.enable("false")) multiplexer_13 (
    .in0(multiplexer_3_out), .in1(multiplexer_5_out), .out(multiplexer_13_out), .sel(not_1_out[1]));
  Multiplexer #(.enable("false")) multiplexer_14 (
    .in0(multiplexer_4_out), .in1(multiplexer_6_out), .out(multiplexer_14_out), .sel(not_1_out[1]));
  Multiplexer #(.enable("false")) multiplexer_15 (
    .in0(multiplexer_5_out), .in1(multiplexer_7_out), .out(multiplexer_15_out), .sel(not_1_out[1]));
  Multiplexer #(.enable("false")) multiplexer_16 (
    .in0(multiplexer_6_out), .in1(multiplexer_8_out), .out(multiplexer_16_out), .sel(not_1_out[1]));
  Multiplexer #(.enable("false")) multiplexer_17 (
    .in0(1'b0), .in1(multiplexer_9_out), .out(out_3[0]), .sel(not_1_out[2]));
  Multiplexer #(.enable("false")) multiplexer_18 (
    .in0(1'b0), .in1(multiplexer_10_out), .out(out_3[1]), .sel(not_1_out[2]));
  Multiplexer #(.enable("false")) multiplexer_19 (
    .in0(1'b0), .in1(multiplexer_11_out), .out(out_3[2]), .sel(not_1_out[2]));
  Multiplexer #(.enable("false")) multiplexer_20 (
    .in0(1'b0), .in1(multiplexer_12_out), .out(out_3[3]), .sel(not_1_out[2]));
  Multiplexer #(.enable("false")) multiplexer_21 (
    .in0(multiplexer_9_out), .in1(multiplexer_13_out), .out(out_3[4]), .sel(not_1_out[2]));
  Multiplexer #(.enable("false")) multiplexer_22 (
    .in0(multiplexer_10_out), .in1(multiplexer_14_out), .out(out_3[5]), .sel(not_1_out[2]));
  Multiplexer #(.enable("false")) multiplexer_23 (
    .in0(multiplexer_11_out), .in1(multiplexer_15_out), .out(out_3[6]), .sel(not_1_out[2]));
  Multiplexer #(.enable("false")) multiplexer_24 (
    .in0(multiplexer_12_out), .in1(multiplexer_16_out), .out(out_3[7]), .sel(not_1_out[2]));
  BitAdder bitadder_1 (.in0(out_3), .out(bitadder_1_out));
  BitAdder bitadder_2 (.in0(in_1), .out(bitadder_2_out));
  Comparator #(.width(4), .mode("unsigned")) comparator_1 (
    .a(bitadder_1_out), .b(bitadder_2_out), .lt(out_4));  // open: gt, eq
endmodule

module L_Shift_Right (
  input  [2:0] in_1,
  input  [7:0] in_2,
  output [7:0] out_3
);

  wire multiplexer_1_out, multiplexer_2_out, multiplexer_3_out, multiplexer_4_out, multiplexer_5_out,
       multiplexer_6_out, multiplexer_7_out, multiplexer_8_out, multiplexer_9_out, multiplexer_10_out,
       multiplexer_11_out, multiplexer_12_out, multiplexer_13_out, multiplexer_14_out, multiplexer_15_out,
       multiplexer_16_out, not_1_out, not_2_out, not_3_out;

  not not_1 (not_1_out, in_1[2]);
  not not_2 (not_2_out, in_1[1]);
  not not_3 (not_3_out, in_1[0]);
  Multiplexer #(.enable("false")) multiplexer_1 (.in0(1'b0), .in1(in_2[7]), .out(multiplexer_1_out), .sel(not_3_out));
  Multiplexer #(.enable("false")) multiplexer_2 (
    .in0(in_2[7]), .in1(in_2[6]), .out(multiplexer_2_out), .sel(not_3_out));
  Multiplexer #(.enable("false")) multiplexer_3 (
    .in0(in_2[6]), .in1(in_2[5]), .out(multiplexer_3_out), .sel(not_3_out));
  Multiplexer #(.enable("false")) multiplexer_4 (
    .in0(in_2[5]), .in1(in_2[4]), .out(multiplexer_4_out), .sel(not_3_out));
  Multiplexer #(.enable("false")) multiplexer_5 (
    .in0(in_2[4]), .in1(in_2[3]), .out(multiplexer_5_out), .sel(not_3_out));
  Multiplexer #(.enable("false")) multiplexer_6 (
    .in0(in_2[3]), .in1(in_2[2]), .out(multiplexer_6_out), .sel(not_3_out));
  Multiplexer #(.enable("false")) multiplexer_7 (
    .in0(in_2[2]), .in1(in_2[1]), .out(multiplexer_7_out), .sel(not_3_out));
  Multiplexer #(.enable("false")) multiplexer_8 (
    .in0(in_2[1]), .in1(in_2[0]), .out(multiplexer_8_out), .sel(not_3_out));
  Multiplexer #(.enable("false")) multiplexer_9 (
    .in0(1'b0), .in1(multiplexer_1_out), .out(multiplexer_9_out), .sel(not_2_out));
  Multiplexer #(.enable("false")) multiplexer_10 (
    .in0(1'b0), .in1(multiplexer_2_out), .out(multiplexer_10_out), .sel(not_2_out));
  Multiplexer #(.enable("false")) multiplexer_11 (
    .in0(multiplexer_1_out), .in1(multiplexer_3_out), .out(multiplexer_11_out), .sel(not_2_out));
  Multiplexer #(.enable("false")) multiplexer_12 (
    .in0(multiplexer_2_out), .in1(multiplexer_4_out), .out(multiplexer_12_out), .sel(not_2_out));
  Multiplexer #(.enable("false")) multiplexer_13 (
    .in0(multiplexer_3_out), .in1(multiplexer_5_out), .out(multiplexer_13_out), .sel(not_2_out));
  Multiplexer #(.enable("false")) multiplexer_14 (
    .in0(multiplexer_4_out), .in1(multiplexer_6_out), .out(multiplexer_14_out), .sel(not_2_out));
  Multiplexer #(.enable("false")) multiplexer_15 (
    .in0(multiplexer_5_out), .in1(multiplexer_7_out), .out(multiplexer_15_out), .sel(not_2_out));
  Multiplexer #(.enable("false")) multiplexer_16 (
    .in0(multiplexer_6_out), .in1(multiplexer_8_out), .out(multiplexer_16_out), .sel(not_2_out));
  Multiplexer #(.enable("false")) multiplexer_17 (.in0(1'b0), .in1(multiplexer_9_out), .out(out_3[7]), .sel(not_1_out));
  Multiplexer #(.enable("false")) multiplexer_18 (
    .in0(1'b0), .in1(multiplexer_10_out), .out(out_3[6]), .sel(not_1_out));
  Multiplexer #(.enable("false")) multiplexer_19 (
    .in0(1'b0), .in1(multiplexer_11_out), .out(out_3[5]), .sel(not_1_out));
  Multiplexer #(.enable("false")) multiplexer_20 (
    .in0(1'b0), .in1(multiplexer_12_out), .out(out_3[4]), .sel(not_1_out));
  Multiplexer #(.enable("false")) multiplexer_21 (
    .in0(multiplexer_9_out), .in1(multiplexer_13_out), .out(out_3[3]), .sel(not_1_out));
  Multiplexer #(.enable("false")) multiplexer_22 (
    .in0(multiplexer_10_out), .in1(multiplexer_14_out), .out(out_3[2]), .sel(not_1_out));
  Multiplexer #(.enable("false")) multiplexer_23 (
    .in0(multiplexer_11_out), .in1(multiplexer_15_out), .out(out_3[1]), .sel(not_1_out));
  Multiplexer #(.enable("false")) multiplexer_24 (
    .in0(multiplexer_12_out), .in1(multiplexer_16_out), .out(out_3[0]), .sel(not_1_out));
endmodule

module L_Shift_Left (
  input  [2:0] in_1,
  input  [7:0] in_2,
  output [7:0] out_3
);

  wire multiplexer_1_out, multiplexer_2_out, multiplexer_3_out, multiplexer_4_out, multiplexer_5_out,
       multiplexer_6_out, multiplexer_7_out, multiplexer_8_out, multiplexer_9_out, multiplexer_10_out,
       multiplexer_11_out, multiplexer_12_out, multiplexer_13_out, multiplexer_14_out, multiplexer_15_out,
       multiplexer_16_out, not_1_out, not_2_out, not_3_out;

  not not_1 (not_1_out, in_1[2]);
  not not_2 (not_2_out, in_1[1]);
  not not_3 (not_3_out, in_1[0]);
  Multiplexer #(.enable("false")) multiplexer_1 (.in0(1'b0), .in1(in_2[0]), .out(multiplexer_1_out), .sel(not_3_out));
  Multiplexer #(.enable("false")) multiplexer_2 (
    .in0(in_2[0]), .in1(in_2[1]), .out(multiplexer_2_out), .sel(not_3_out));
  Multiplexer #(.enable("false")) multiplexer_3 (
    .in0(in_2[1]), .in1(in_2[2]), .out(multiplexer_3_out), .sel(not_3_out));
  Multiplexer #(.enable("false")) multiplexer_4 (
    .in0(in_2[2]), .in1(in_2[3]), .out(multiplexer_4_out), .sel(not_3_out));
  Multiplexer #(.enable("false")) multiplexer_5 (
    .in0(in_2[3]), .in1(in_2[4]), .out(multiplexer_5_out), .sel(not_3_out));
  Multiplexer #(.enable("false")) multiplexer_6 (
    .in0(in_2[4]), .in1(in_2[5]), .out(multiplexer_6_out), .sel(not_3_out));
  Multiplexer #(.enable("false")) multiplexer_7 (
    .in0(in_2[5]), .in1(in_2[6]), .out(multiplexer_7_out), .sel(not_3_out));
  Multiplexer #(.enable("false")) multiplexer_8 (
    .in0(in_2[6]), .in1(in_2[7]), .out(multiplexer_8_out), .sel(not_3_out));
  Multiplexer #(.enable("false")) multiplexer_9 (
    .in0(1'b0), .in1(multiplexer_1_out), .out(multiplexer_9_out), .sel(not_2_out));
  Multiplexer #(.enable("false")) multiplexer_10 (
    .in0(1'b0), .in1(multiplexer_2_out), .out(multiplexer_10_out), .sel(not_2_out));
  Multiplexer #(.enable("false")) multiplexer_11 (
    .in0(multiplexer_1_out), .in1(multiplexer_3_out), .out(multiplexer_11_out), .sel(not_2_out));
  Multiplexer #(.enable("false")) multiplexer_12 (
    .in0(multiplexer_2_out), .in1(multiplexer_4_out), .out(multiplexer_12_out), .sel(not_2_out));
  Multiplexer #(.enable("false")) multiplexer_13 (
    .in0(multiplexer_3_out), .in1(multiplexer_5_out), .out(multiplexer_13_out), .sel(not_2_out));
  Multiplexer #(.enable("false")) multiplexer_14 (
    .in0(multiplexer_4_out), .in1(multiplexer_6_out), .out(multiplexer_14_out), .sel(not_2_out));
  Multiplexer #(.enable("false")) multiplexer_15 (
    .in0(multiplexer_5_out), .in1(multiplexer_7_out), .out(multiplexer_15_out), .sel(not_2_out));
  Multiplexer #(.enable("false")) multiplexer_16 (
    .in0(multiplexer_6_out), .in1(multiplexer_8_out), .out(multiplexer_16_out), .sel(not_2_out));
  Multiplexer #(.enable("false")) multiplexer_17 (.in0(1'b0), .in1(multiplexer_9_out), .out(out_3[0]), .sel(not_1_out));
  Multiplexer #(.enable("false")) multiplexer_18 (
    .in0(1'b0), .in1(multiplexer_10_out), .out(out_3[1]), .sel(not_1_out));
  Multiplexer #(.enable("false")) multiplexer_19 (
    .in0(1'b0), .in1(multiplexer_11_out), .out(out_3[2]), .sel(not_1_out));
  Multiplexer #(.enable("false")) multiplexer_20 (
    .in0(1'b0), .in1(multiplexer_12_out), .out(out_3[3]), .sel(not_1_out));
  Multiplexer #(.enable("false")) multiplexer_21 (
    .in0(multiplexer_9_out), .in1(multiplexer_13_out), .out(out_3[4]), .sel(not_1_out));
  Multiplexer #(.enable("false")) multiplexer_22 (
    .in0(multiplexer_10_out), .in1(multiplexer_14_out), .out(out_3[5]), .sel(not_1_out));
  Multiplexer #(.enable("false")) multiplexer_23 (
    .in0(multiplexer_11_out), .in1(multiplexer_15_out), .out(out_3[6]), .sel(not_1_out));
  Multiplexer #(.enable("false")) multiplexer_24 (
    .in0(multiplexer_12_out), .in1(multiplexer_16_out), .out(out_3[7]), .sel(not_1_out));
endmodule

module A_Shift_Right (
  input  [2:0] in_1,
  input  [7:0] in_2,
  output [7:0] out_3
);

  wire multiplexer_1_out, multiplexer_2_out, multiplexer_3_out, multiplexer_4_out, multiplexer_5_out,
       multiplexer_6_out, multiplexer_7_out, multiplexer_8_out, multiplexer_9_out, multiplexer_10_out,
       multiplexer_11_out, multiplexer_12_out, multiplexer_13_out, multiplexer_14_out, multiplexer_15_out,
       multiplexer_16_out, not_1_out, not_2_out, not_3_out;

  not not_1 (not_1_out, in_1[2]);
  not not_2 (not_2_out, in_1[1]);
  not not_3 (not_3_out, in_1[0]);
  Multiplexer #(.enable("false")) multiplexer_1 (
    .in0(in_2[0]), .in1(in_2[7]), .out(multiplexer_1_out), .sel(not_3_out));
  Multiplexer #(.enable("false")) multiplexer_2 (
    .in0(in_2[7]), .in1(in_2[6]), .out(multiplexer_2_out), .sel(not_3_out));
  Multiplexer #(.enable("false")) multiplexer_3 (
    .in0(in_2[6]), .in1(in_2[5]), .out(multiplexer_3_out), .sel(not_3_out));
  Multiplexer #(.enable("false")) multiplexer_4 (
    .in0(in_2[5]), .in1(in_2[4]), .out(multiplexer_4_out), .sel(not_3_out));
  Multiplexer #(.enable("false")) multiplexer_5 (
    .in0(in_2[4]), .in1(in_2[3]), .out(multiplexer_5_out), .sel(not_3_out));
  Multiplexer #(.enable("false")) multiplexer_6 (
    .in0(in_2[3]), .in1(in_2[2]), .out(multiplexer_6_out), .sel(not_3_out));
  Multiplexer #(.enable("false")) multiplexer_7 (
    .in0(in_2[2]), .in1(in_2[1]), .out(multiplexer_7_out), .sel(not_3_out));
  Multiplexer #(.enable("false")) multiplexer_8 (
    .in0(in_2[1]), .in1(in_2[0]), .out(multiplexer_8_out), .sel(not_3_out));
  Multiplexer #(.enable("false")) multiplexer_9 (
    .in0(in_2[0]), .in1(multiplexer_1_out), .out(multiplexer_9_out), .sel(not_2_out));
  Multiplexer #(.enable("false")) multiplexer_10 (
    .in0(in_2[0]), .in1(multiplexer_2_out), .out(multiplexer_10_out), .sel(not_2_out));
  Multiplexer #(.enable("false")) multiplexer_11 (
    .in0(multiplexer_1_out), .in1(multiplexer_3_out), .out(multiplexer_11_out), .sel(not_2_out));
  Multiplexer #(.enable("false")) multiplexer_12 (
    .in0(multiplexer_2_out), .in1(multiplexer_4_out), .out(multiplexer_12_out), .sel(not_2_out));
  Multiplexer #(.enable("false")) multiplexer_13 (
    .in0(multiplexer_3_out), .in1(multiplexer_5_out), .out(multiplexer_13_out), .sel(not_2_out));
  Multiplexer #(.enable("false")) multiplexer_14 (
    .in0(multiplexer_4_out), .in1(multiplexer_6_out), .out(multiplexer_14_out), .sel(not_2_out));
  Multiplexer #(.enable("false")) multiplexer_15 (
    .in0(multiplexer_5_out), .in1(multiplexer_7_out), .out(multiplexer_15_out), .sel(not_2_out));
  Multiplexer #(.enable("false")) multiplexer_16 (
    .in0(multiplexer_6_out), .in1(multiplexer_8_out), .out(multiplexer_16_out), .sel(not_2_out));
  Multiplexer #(.enable("false")) multiplexer_17 (
    .in0(in_2[0]), .in1(multiplexer_9_out), .out(out_3[7]), .sel(not_1_out));
  Multiplexer #(.enable("false")) multiplexer_18 (
    .in0(in_2[0]), .in1(multiplexer_10_out), .out(out_3[6]), .sel(not_1_out));
  Multiplexer #(.enable("false")) multiplexer_19 (
    .in0(in_2[0]), .in1(multiplexer_11_out), .out(out_3[5]), .sel(not_1_out));
  Multiplexer #(.enable("false")) multiplexer_20 (
    .in0(in_2[0]), .in1(multiplexer_12_out), .out(out_3[4]), .sel(not_1_out));
  Multiplexer #(.enable("false")) multiplexer_21 (
    .in0(multiplexer_9_out), .in1(multiplexer_13_out), .out(out_3[3]), .sel(not_1_out));
  Multiplexer #(.enable("false")) multiplexer_22 (
    .in0(multiplexer_10_out), .in1(multiplexer_14_out), .out(out_3[2]), .sel(not_1_out));
  Multiplexer #(.enable("false")) multiplexer_23 (
    .in0(multiplexer_11_out), .in1(multiplexer_15_out), .out(out_3[1]), .sel(not_1_out));
  Multiplexer #(.enable("false")) multiplexer_24 (
    .in0(multiplexer_12_out), .in1(multiplexer_16_out), .out(out_3[0]), .sel(not_1_out));
endmodule

module Cycle_Shift_Right (
  input  [2:0] in_1,
  input  [7:0] in_2,
  output [7:0] out_3
);

  wire multiplexer_1_out, multiplexer_2_out, multiplexer_3_out, multiplexer_4_out, multiplexer_5_out,
       multiplexer_6_out, multiplexer_7_out, multiplexer_8_out, multiplexer_9_out, multiplexer_10_out,
       multiplexer_11_out, multiplexer_12_out, multiplexer_13_out, multiplexer_14_out, multiplexer_15_out,
       multiplexer_16_out, not_1_out, not_2_out, not_3_out;

  not not_1 (not_1_out, in_1[2]);
  not not_2 (not_2_out, in_1[1]);
  not not_3 (not_3_out, in_1[0]);
  Multiplexer #(.enable("false")) multiplexer_1 (
    .in0(in_2[0]), .in1(in_2[7]), .out(multiplexer_1_out), .sel(not_3_out));
  Multiplexer #(.enable("false")) multiplexer_2 (
    .in0(in_2[7]), .in1(in_2[6]), .out(multiplexer_2_out), .sel(not_3_out));
  Multiplexer #(.enable("false")) multiplexer_3 (
    .in0(in_2[6]), .in1(in_2[5]), .out(multiplexer_3_out), .sel(not_3_out));
  Multiplexer #(.enable("false")) multiplexer_4 (
    .in0(in_2[5]), .in1(in_2[4]), .out(multiplexer_4_out), .sel(not_3_out));
  Multiplexer #(.enable("false")) multiplexer_5 (
    .in0(in_2[4]), .in1(in_2[3]), .out(multiplexer_5_out), .sel(not_3_out));
  Multiplexer #(.enable("false")) multiplexer_6 (
    .in0(in_2[3]), .in1(in_2[2]), .out(multiplexer_6_out), .sel(not_3_out));
  Multiplexer #(.enable("false")) multiplexer_7 (
    .in0(in_2[2]), .in1(in_2[1]), .out(multiplexer_7_out), .sel(not_3_out));
  Multiplexer #(.enable("false")) multiplexer_8 (
    .in0(in_2[1]), .in1(in_2[0]), .out(multiplexer_8_out), .sel(not_3_out));
  Multiplexer #(.enable("false")) multiplexer_9 (
    .in0(multiplexer_7_out), .in1(multiplexer_1_out), .out(multiplexer_9_out), .sel(not_2_out));
  Multiplexer #(.enable("false")) multiplexer_10 (
    .in0(multiplexer_8_out), .in1(multiplexer_2_out), .out(multiplexer_10_out), .sel(not_2_out));
  Multiplexer #(.enable("false")) multiplexer_11 (
    .in0(multiplexer_1_out), .in1(multiplexer_3_out), .out(multiplexer_11_out), .sel(not_2_out));
  Multiplexer #(.enable("false")) multiplexer_12 (
    .in0(multiplexer_2_out), .in1(multiplexer_4_out), .out(multiplexer_12_out), .sel(not_2_out));
  Multiplexer #(.enable("false")) multiplexer_13 (
    .in0(multiplexer_3_out), .in1(multiplexer_5_out), .out(multiplexer_13_out), .sel(not_2_out));
  Multiplexer #(.enable("false")) multiplexer_14 (
    .in0(multiplexer_4_out), .in1(multiplexer_6_out), .out(multiplexer_14_out), .sel(not_2_out));
  Multiplexer #(.enable("false")) multiplexer_15 (
    .in0(multiplexer_5_out), .in1(multiplexer_7_out), .out(multiplexer_15_out), .sel(not_2_out));
  Multiplexer #(.enable("false")) multiplexer_16 (
    .in0(multiplexer_6_out), .in1(multiplexer_8_out), .out(multiplexer_16_out), .sel(not_2_out));
  Multiplexer #(.enable("false")) multiplexer_17 (
    .in0(multiplexer_13_out), .in1(multiplexer_9_out), .out(out_3[7]), .sel(not_1_out));
  Multiplexer #(.enable("false")) multiplexer_18 (
    .in0(multiplexer_14_out), .in1(multiplexer_10_out), .out(out_3[6]), .sel(not_1_out));
  Multiplexer #(.enable("false")) multiplexer_19 (
    .in0(multiplexer_15_out), .in1(multiplexer_11_out), .out(out_3[5]), .sel(not_1_out));
  Multiplexer #(.enable("false")) multiplexer_20 (
    .in0(multiplexer_16_out), .in1(multiplexer_12_out), .out(out_3[4]), .sel(not_1_out));
  Multiplexer #(.enable("false")) multiplexer_21 (
    .in0(multiplexer_9_out), .in1(multiplexer_13_out), .out(out_3[3]), .sel(not_1_out));
  Multiplexer #(.enable("false")) multiplexer_22 (
    .in0(multiplexer_10_out), .in1(multiplexer_14_out), .out(out_3[2]), .sel(not_1_out));
  Multiplexer #(.enable("false")) multiplexer_23 (
    .in0(multiplexer_11_out), .in1(multiplexer_15_out), .out(out_3[1]), .sel(not_1_out));
  Multiplexer #(.enable("false")) multiplexer_24 (
    .in0(multiplexer_12_out), .in1(multiplexer_16_out), .out(out_3[0]), .sel(not_1_out));
endmodule

module Cycle_Shift_Left (
  input  [2:0] in_1,
  input  [7:0] in_2,
  output [7:0] out_3
);

  wire multiplexer_1_out, multiplexer_2_out, multiplexer_3_out, multiplexer_4_out, multiplexer_5_out,
       multiplexer_6_out, multiplexer_7_out, multiplexer_8_out, multiplexer_9_out, multiplexer_10_out,
       multiplexer_11_out, multiplexer_12_out, multiplexer_13_out, multiplexer_14_out, multiplexer_15_out,
       multiplexer_16_out, not_1_out, not_2_out, not_3_out;

  not not_1 (not_1_out, in_1[2]);
  not not_2 (not_2_out, in_1[1]);
  not not_3 (not_3_out, in_1[0]);
  Multiplexer #(.enable("false")) multiplexer_1 (
    .in0(in_2[7]), .in1(in_2[0]), .out(multiplexer_1_out), .sel(not_3_out));
  Multiplexer #(.enable("false")) multiplexer_2 (
    .in0(in_2[0]), .in1(in_2[1]), .out(multiplexer_2_out), .sel(not_3_out));
  Multiplexer #(.enable("false")) multiplexer_3 (
    .in0(in_2[1]), .in1(in_2[2]), .out(multiplexer_3_out), .sel(not_3_out));
  Multiplexer #(.enable("false")) multiplexer_4 (
    .in0(in_2[2]), .in1(in_2[3]), .out(multiplexer_4_out), .sel(not_3_out));
  Multiplexer #(.enable("false")) multiplexer_5 (
    .in0(in_2[3]), .in1(in_2[4]), .out(multiplexer_5_out), .sel(not_3_out));
  Multiplexer #(.enable("false")) multiplexer_6 (
    .in0(in_2[4]), .in1(in_2[5]), .out(multiplexer_6_out), .sel(not_3_out));
  Multiplexer #(.enable("false")) multiplexer_7 (
    .in0(in_2[5]), .in1(in_2[6]), .out(multiplexer_7_out), .sel(not_3_out));
  Multiplexer #(.enable("false")) multiplexer_8 (
    .in0(in_2[6]), .in1(in_2[7]), .out(multiplexer_8_out), .sel(not_3_out));
  Multiplexer #(.enable("false")) multiplexer_9 (
    .in0(multiplexer_7_out), .in1(multiplexer_1_out), .out(multiplexer_9_out), .sel(not_2_out));
  Multiplexer #(.enable("false")) multiplexer_10 (
    .in0(multiplexer_8_out), .in1(multiplexer_2_out), .out(multiplexer_10_out), .sel(not_2_out));
  Multiplexer #(.enable("false")) multiplexer_11 (
    .in0(multiplexer_1_out), .in1(multiplexer_3_out), .out(multiplexer_11_out), .sel(not_2_out));
  Multiplexer #(.enable("false")) multiplexer_12 (
    .in0(multiplexer_2_out), .in1(multiplexer_4_out), .out(multiplexer_12_out), .sel(not_2_out));
  Multiplexer #(.enable("false")) multiplexer_13 (
    .in0(multiplexer_3_out), .in1(multiplexer_5_out), .out(multiplexer_13_out), .sel(not_2_out));
  Multiplexer #(.enable("false")) multiplexer_14 (
    .in0(multiplexer_4_out), .in1(multiplexer_6_out), .out(multiplexer_14_out), .sel(not_2_out));
  Multiplexer #(.enable("false")) multiplexer_15 (
    .in0(multiplexer_5_out), .in1(multiplexer_7_out), .out(multiplexer_15_out), .sel(not_2_out));
  Multiplexer #(.enable("false")) multiplexer_16 (
    .in0(multiplexer_6_out), .in1(multiplexer_8_out), .out(multiplexer_16_out), .sel(not_2_out));
  Multiplexer #(.enable("false")) multiplexer_17 (
    .in0(multiplexer_13_out), .in1(multiplexer_9_out), .out(out_3[0]), .sel(not_1_out));
  Multiplexer #(.enable("false")) multiplexer_18 (
    .in0(multiplexer_14_out), .in1(multiplexer_10_out), .out(out_3[1]), .sel(not_1_out));
  Multiplexer #(.enable("false")) multiplexer_19 (
    .in0(multiplexer_15_out), .in1(multiplexer_11_out), .out(out_3[2]), .sel(not_1_out));
  Multiplexer #(.enable("false")) multiplexer_20 (
    .in0(multiplexer_16_out), .in1(multiplexer_12_out), .out(out_3[3]), .sel(not_1_out));
  Multiplexer #(.enable("false")) multiplexer_21 (
    .in0(multiplexer_9_out), .in1(multiplexer_13_out), .out(out_3[4]), .sel(not_1_out));
  Multiplexer #(.enable("false")) multiplexer_22 (
    .in0(multiplexer_10_out), .in1(multiplexer_14_out), .out(out_3[5]), .sel(not_1_out));
  Multiplexer #(.enable("false")) multiplexer_23 (
    .in0(multiplexer_11_out), .in1(multiplexer_15_out), .out(out_3[6]), .sel(not_1_out));
  Multiplexer #(.enable("false")) multiplexer_24 (
    .in0(multiplexer_12_out), .in1(multiplexer_16_out), .out(out_3[7]), .sel(not_1_out));
endmodule

module Equal (
  input  [7:0] in_1,
  input  [7:0] in_2,
  output out_3
);

  wire [7:0] xor_1_out;

  assign xor_1_out = in_1 ^ in_2;  // XOR_Gate xor_1, 8 bits wide
  LOGIC_NOT logic_not_1 (.in_1(xor_1_out), .out_2(out_3));
endmodule

module Not_Equal (
  input  [7:0] in_1,
  input  [7:0] in_2,
  output out_3
);

  wire logic_not_1_out_2;
  wire [7:0] xor_1_out;

  assign xor_1_out = in_1 ^ in_2;  // XOR_Gate xor_1, 8 bits wide
  LOGIC_NOT logic_not_1 (.in_1(xor_1_out), .out_2(logic_not_1_out_2));
  not not_1 (out_3, logic_not_1_out_2);
endmodule

module More (
  input  in_1,
  input  in_2,
  output out_3
);

  wire not_1_out;

  not not_1 (not_1_out, in_2);
  and and_1 (out_3, in_1, not_1_out);
endmodule

module More_of_Equal (
  input  in_1,
  input  in_2,
  output out_3
);

  wire and_1_out, not_1_out, xnor_1_out;

  not not_1 (not_1_out, in_2);
  and and_1 (and_1_out, in_1, not_1_out);
  xnor xnor_1 (xnor_1_out, in_1, in_2);
  or or_1 (out_3, and_1_out, xnor_1_out);
endmodule

module More_8_Unsigned (
  input  [7:0] in_1,
  input  [7:0] in_2,
  output out_3
);

  wire and_1_out, and_2_out, and_3_out, and_4_out, and_5_out, and_6_out, and_7_out, more_1_out_3,
       more_2_out_3, more_3_out_3, more_4_out_3, more_5_out_3, more_6_out_3, more_7_out_3, more_8_out_3,
       more_of_equal_1_out_3, more_of_equal_2_out_3, more_of_equal_3_out_3, more_of_equal_4_out_3,
       more_of_equal_5_out_3, more_of_equal_6_out_3, more_of_equal_7_out_3;

  and and_1 (and_1_out, more_1_out_3, more_of_equal_1_out_3, more_of_equal_2_out_3, more_of_equal_3_out_3, more_of_equal_4_out_3, more_of_equal_5_out_3, more_of_equal_6_out_3, more_of_equal_7_out_3);
  More more_1 (.in_1(in_1[0]), .in_2(in_2[0]), .out_3(more_1_out_3));
  More more_2 (.in_1(in_1[1]), .in_2(in_2[1]), .out_3(more_2_out_3));
  More_of_Equal more_of_equal_1 (.in_1(in_1[1]), .in_2(in_2[1]), .out_3(more_of_equal_1_out_3));
  and and_2 (and_2_out, more_of_equal_7_out_3, more_of_equal_6_out_3, more_of_equal_5_out_3, more_of_equal_4_out_3, more_of_equal_3_out_3, more_of_equal_2_out_3, more_2_out_3);
  More more_3 (.in_1(in_1[2]), .in_2(in_2[2]), .out_3(more_3_out_3));
  More_of_Equal more_of_equal_2 (.in_1(in_1[2]), .in_2(in_2[2]), .out_3(more_of_equal_2_out_3));
  and and_3 (and_3_out, more_of_equal_7_out_3, more_of_equal_6_out_3, more_of_equal_5_out_3, more_of_equal_4_out_3, more_of_equal_3_out_3, more_3_out_3);
  More_of_Equal more_of_equal_3 (.in_1(in_1[3]), .in_2(in_2[3]), .out_3(more_of_equal_3_out_3));
  More more_4 (.in_1(in_1[3]), .in_2(in_2[3]), .out_3(more_4_out_3));
  and and_4 (and_4_out, more_of_equal_7_out_3, more_of_equal_6_out_3, more_of_equal_5_out_3, more_of_equal_4_out_3, more_4_out_3);
  or or_1 (out_3, and_1_out, and_2_out, and_3_out, and_4_out, and_5_out, and_6_out, and_7_out, more_8_out_3);
  More_of_Equal more_of_equal_4 (.in_1(in_1[4]), .in_2(in_2[4]), .out_3(more_of_equal_4_out_3));
  More more_5 (.in_1(in_1[4]), .in_2(in_2[4]), .out_3(more_5_out_3));
  and and_5 (and_5_out, more_of_equal_7_out_3, more_of_equal_6_out_3, more_of_equal_5_out_3, more_5_out_3);
  More_of_Equal more_of_equal_5 (.in_1(in_1[5]), .in_2(in_2[5]), .out_3(more_of_equal_5_out_3));
  More more_6 (.in_1(in_1[5]), .in_2(in_2[5]), .out_3(more_6_out_3));
  and and_6 (and_6_out, more_of_equal_7_out_3, more_of_equal_6_out_3, more_6_out_3);
  More_of_Equal more_of_equal_6 (.in_1(in_1[6]), .in_2(in_2[6]), .out_3(more_of_equal_6_out_3));
  More more_7 (.in_1(in_1[6]), .in_2(in_2[6]), .out_3(more_7_out_3));
  and and_7 (and_7_out, more_of_equal_7_out_3, more_7_out_3);
  More more_8 (.in_1(in_1[7]), .in_2(in_2[7]), .out_3(more_8_out_3));
  More_of_Equal more_of_equal_7 (.in_1(in_1[7]), .in_2(in_2[7]), .out_3(more_of_equal_7_out_3));
endmodule

module More_8_Signed (
  input  [7:0] in_1,
  input  [7:0] in_2,
  output out_3
);

  wire and_1_out, and_2_out, and_3_out, and_4_out, and_5_out, and_6_out, and_7_out, more_1_out_3,
       more_2_out_3, more_3_out_3, more_4_out_3, more_5_out_3, more_6_out_3, more_7_out_3, more_8_out_3,
       more_of_equal_1_out_3, more_of_equal_2_out_3, more_of_equal_3_out_3, more_of_equal_4_out_3,
       more_of_equal_5_out_3, more_of_equal_6_out_3, more_of_equal_7_out_3;

  and and_1 (and_1_out, more_1_out_3, more_of_equal_1_out_3, more_of_equal_2_out_3, more_of_equal_3_out_3, more_of_equal_4_out_3, more_of_equal_5_out_3, more_of_equal_6_out_3, more_of_equal_7_out_3);
  More more_1 (.in_1(in_1[0]), .in_2(in_2[0]), .out_3(more_1_out_3));
  More_of_Equal more_of_equal_1 (.in_1(in_1[1]), .in_2(in_2[1]), .out_3(more_of_equal_1_out_3));
  More more_2 (.in_1(in_1[1]), .in_2(in_2[1]), .out_3(more_2_out_3));
  and and_2 (and_2_out, more_of_equal_7_out_3, more_of_equal_6_out_3, more_of_equal_5_out_3, more_of_equal_4_out_3, more_of_equal_3_out_3, more_of_equal_2_out_3, more_2_out_3);
  More more_3 (.in_1(in_1[2]), .in_2(in_2[2]), .out_3(more_3_out_3));
  More_of_Equal more_of_equal_2 (.in_1(in_1[2]), .in_2(in_2[2]), .out_3(more_of_equal_2_out_3));
  and and_3 (and_3_out, more_of_equal_7_out_3, more_of_equal_6_out_3, more_of_equal_5_out_3, more_of_equal_4_out_3, more_of_equal_3_out_3, more_3_out_3);
  More_of_Equal more_of_equal_3 (.in_1(in_1[3]), .in_2(in_2[3]), .out_3(more_of_equal_3_out_3));
  More more_4 (.in_1(in_1[3]), .in_2(in_2[3]), .out_3(more_4_out_3));
  and and_4 (and_4_out, more_of_equal_7_out_3, more_of_equal_6_out_3, more_of_equal_5_out_3, more_of_equal_4_out_3, more_4_out_3);
  or or_1 (out_3, and_1_out, and_2_out, and_3_out, and_4_out, and_5_out, and_6_out, and_7_out, more_8_out_3);
  More_of_Equal more_of_equal_4 (.in_1(in_1[4]), .in_2(in_2[4]), .out_3(more_of_equal_4_out_3));
  More more_5 (.in_1(in_1[4]), .in_2(in_2[4]), .out_3(more_5_out_3));
  and and_5 (and_5_out, more_of_equal_7_out_3, more_of_equal_6_out_3, more_of_equal_5_out_3, more_5_out_3);
  More more_6 (.in_1(in_1[5]), .in_2(in_2[5]), .out_3(more_6_out_3));
  More_of_Equal more_of_equal_5 (.in_1(in_1[5]), .in_2(in_2[5]), .out_3(more_of_equal_5_out_3));
  and and_6 (and_6_out, more_of_equal_7_out_3, more_of_equal_6_out_3, more_6_out_3);
  More_of_Equal more_of_equal_6 (.in_1(in_1[6]), .in_2(in_2[6]), .out_3(more_of_equal_6_out_3));
  More more_7 (.in_1(in_1[6]), .in_2(in_2[6]), .out_3(more_7_out_3));
  and and_7 (and_7_out, more_of_equal_7_out_3, more_7_out_3);
  More_of_Equal more_of_equal_7 (.in_1(in_2[7]), .in_2(in_1[7]), .out_3(more_of_equal_7_out_3));
  More more_8 (.in_1(in_2[7]), .in_2(in_1[7]), .out_3(more_8_out_3));
endmodule

module Less_8_Unsigned (
  input  [7:0] in_1,
  input  [7:0] in_2,
  output out_3
);

  wire more_8_unsigned_1_out_3, not_1_out, not_equal_1_out_3;

  More_8_Unsigned more_8_unsigned_1 (.in_1(in_1), .in_2(in_2), .out_3(more_8_unsigned_1_out_3));
  Not_Equal not_equal_1 (.in_1(in_1), .in_2(in_2), .out_3(not_equal_1_out_3));
  not not_1 (not_1_out, more_8_unsigned_1_out_3);
  and and_1 (out_3, not_1_out, not_equal_1_out_3);
endmodule

module Less_8_Signed (
  input  [7:0] in_1,
  input  [7:0] in_2,
  output out_3
);

  wire more_8_signed_1_out_3, not_1_out, not_equal_1_out_3;

  Not_Equal not_equal_1 (.in_1(in_1), .in_2(in_2), .out_3(not_equal_1_out_3));
  More_8_Signed more_8_signed_1 (.in_1(in_1), .in_2(in_2), .out_3(more_8_signed_1_out_3));
  not not_1 (not_1_out, more_8_signed_1_out_3);
  and and_1 (out_3, not_1_out, not_equal_1_out_3);
endmodule

module More_or_Equal_8_Unsigned (
  input  [7:0] in_1,
  input  [7:0] in_2,
  output out_3
);

  wire less_8_unsigned_1_out_3;

  not not_1 (out_3, less_8_unsigned_1_out_3);
  Less_8_Unsigned less_8_unsigned_1 (.in_1(in_1), .in_2(in_2), .out_3(less_8_unsigned_1_out_3));
endmodule

module Less_or_Equal_8_Signed (
  input  [7:0] in_1,
  input  [7:0] in_2,
  output out_3
);

  wire more_8_signed_1_out_3;

  More_8_Signed more_8_signed_1 (.in_1(in_1), .in_2(in_2), .out_3(more_8_signed_1_out_3));
  not not_1 (out_3, more_8_signed_1_out_3);
endmodule

module Less_or_Equal_8_Unsigned (
  input  [7:0] in_1,
  input  [7:0] in_2,
  output out_3
);

  wire more_8_unsigned_1_out_3;

  More_8_Unsigned more_8_unsigned_1 (.in_1(in_1), .in_2(in_2), .out_3(more_8_unsigned_1_out_3));
  not not_1 (out_3, more_8_unsigned_1_out_3);
endmodule

module Half_adder (
  input  in_1,
  input  in_2,
  output out_3,
  output out_4
);

  xor xor_1 (out_3, in_1, in_2);
  and and_1 (out_4, in_1, in_2);

  // Notes on the sheet:
  //             Low bit
  //   Overflow
endmodule

module Adder (
  input  in_1,
  input  in_2,
  input  in_3,
  output L,
  output O
);

  wire half_adder_1_out_3, half_adder_1_out_4, half_adder_2_out_4;

  Half_adder half_adder_1 (.in_1(in_2), .in_2(in_3), .out_3(half_adder_1_out_3), .out_4(half_adder_1_out_4));
  Half_adder half_adder_2 (.in_1(in_1), .in_2(half_adder_1_out_3), .out_3(L), .out_4(half_adder_2_out_4));
  or or_1 (O, half_adder_2_out_4, half_adder_1_out_4);
endmodule

module Adder_8 (
  input  [7:0] in_1,
  input  [7:0] in_2,
  output [7:0] out_3,
  output out_4
);

  wire adder_1_o, adder_2_o, adder_3_o, adder_4_o, adder_5_o, adder_6_o, adder_7_o;

  Adder adder_1 (.in_2(in_1[0]), .in_3(in_2[0]), .L(out_3[0]), .O(adder_1_o), .in_1(1'b0));
  Adder adder_2 (.in_2(in_2[1]), .in_3(in_1[1]), .L(out_3[1]), .O(adder_2_o), .in_1(adder_1_o));
  Adder adder_3 (.in_2(in_2[2]), .in_3(in_1[2]), .L(out_3[2]), .O(adder_3_o), .in_1(adder_2_o));
  Adder adder_4 (.in_2(in_2[3]), .in_3(in_1[3]), .L(out_3[3]), .O(adder_4_o), .in_1(adder_3_o));
  Adder adder_5 (.in_2(in_2[4]), .in_3(in_1[4]), .L(out_3[4]), .O(adder_5_o), .in_1(adder_4_o));
  Adder adder_6 (.in_2(in_2[5]), .in_3(in_1[5]), .L(out_3[5]), .O(adder_6_o), .in_1(adder_5_o));
  Adder adder_7 (.in_2(in_2[6]), .in_3(in_1[6]), .L(out_3[6]), .O(adder_7_o), .in_1(adder_6_o));
  Adder adder_8 (.in_2(in_2[7]), .in_3(in_1[7]), .L(out_3[7]), .O(out_4), .in_1(adder_7_o));
endmodule

module Multiply (
  input  [7:0] in_1,
  input  [7:0] in_2,
  output [7:0] out_3,
  output out_4
);

  wire adder_1_cout, adder_2_cout, adder_3_cout, adder_4_cout, adder_5_cout, adder_6_cout, adder_7_cout,
       and_9_out, and_10_out, and_11_out, and_12_out, and_13_out, and_14_out, and_15_out,
       l_a_shift_left_1_out_4, l_a_shift_left_2_out_4, l_a_shift_left_3_out_4, l_a_shift_left_4_out_4,
       l_a_shift_left_5_out_4, l_a_shift_left_6_out_4, l_a_shift_left_7_out_4;
  wire [7:0] adder_1_out, adder_2_out, adder_3_out, adder_4_out, adder_5_out, adder_6_out, and_1_out,
       and_2_out, and_3_out, and_4_out, and_5_out, and_6_out, and_7_out, and_8_out, l_a_shift_left_1_out_3,
       l_a_shift_left_2_out_3, l_a_shift_left_3_out_3, l_a_shift_left_4_out_3, l_a_shift_left_5_out_3,
       l_a_shift_left_6_out_3, l_a_shift_left_7_out_3;

  L_A_Shift_Left l_a_shift_left_1 (
    .in_1(in_1), .out_3(l_a_shift_left_1_out_3), .out_4(l_a_shift_left_1_out_4), .in_2(3'b111));
  L_A_Shift_Left l_a_shift_left_2 (
    .in_1(in_1), .out_3(l_a_shift_left_2_out_3), .out_4(l_a_shift_left_2_out_4), .in_2(3'b110));
  assign and_1_out = l_a_shift_left_1_out_3 & {8{in_2[7]}};  // AND_Gate and_1, 8 bits wide
  L_A_Shift_Left l_a_shift_left_3 (
    .in_1(in_1), .out_3(l_a_shift_left_3_out_3), .out_4(l_a_shift_left_3_out_4), .in_2(3'b101));
  assign and_2_out = l_a_shift_left_2_out_3 & {8{in_2[6]}};  // AND_Gate and_2, 8 bits wide
  L_A_Shift_Left l_a_shift_left_4 (
    .in_1(in_1), .out_3(l_a_shift_left_4_out_3), .out_4(l_a_shift_left_4_out_4), .in_2(3'b100));
  assign and_3_out = l_a_shift_left_3_out_3 & {8{in_2[5]}};  // AND_Gate and_3, 8 bits wide
  L_A_Shift_Left l_a_shift_left_5 (
    .in_1(in_1), .out_3(l_a_shift_left_5_out_3), .out_4(l_a_shift_left_5_out_4), .in_2(3'b011));
  assign and_4_out = l_a_shift_left_4_out_3 & {8{in_2[4]}};  // AND_Gate and_4, 8 bits wide
  L_A_Shift_Left l_a_shift_left_6 (
    .in_1(in_1), .out_3(l_a_shift_left_6_out_3), .out_4(l_a_shift_left_6_out_4), .in_2(3'b010));
  L_A_Shift_Left l_a_shift_left_7 (
    .in_1(in_1), .out_3(l_a_shift_left_7_out_3), .out_4(l_a_shift_left_7_out_4), .in_2(3'b001));
  assign and_5_out = l_a_shift_left_5_out_3 & {8{in_2[3]}};  // AND_Gate and_5, 8 bits wide
  assign and_6_out = l_a_shift_left_6_out_3 & {8{in_2[2]}};  // AND_Gate and_6, 8 bits wide
  assign and_7_out = l_a_shift_left_7_out_3 & {8{in_2[1]}};  // AND_Gate and_7, 8 bits wide
  assign and_8_out = in_1 & {8{in_2[0]}};  // AND_Gate and_8, 8 bits wide
  Adder_part adder_1 (.a(and_8_out), .b(and_7_out), .out(adder_1_out), .cout(adder_1_cout));  // open: cin
  Adder_part adder_2 (.a(adder_1_out), .b(and_6_out), .out(adder_2_out), .cout(adder_2_cout));  // open: cin
  Adder_part adder_3 (.a(adder_2_out), .b(and_5_out), .out(adder_3_out), .cout(adder_3_cout));  // open: cin
  Adder_part adder_4 (.a(adder_3_out), .b(and_4_out), .out(adder_4_out), .cout(adder_4_cout));  // open: cin
  Adder_part adder_5 (.a(adder_4_out), .b(and_3_out), .out(adder_5_out), .cout(adder_5_cout));  // open: cin
  Adder_part adder_6 (.a(adder_5_out), .b(and_2_out), .out(adder_6_out), .cout(adder_6_cout));  // open: cin
  and and_9 (and_9_out, l_a_shift_left_7_out_4, in_2[1]);
  and and_10 (and_10_out, l_a_shift_left_6_out_4, in_2[2]);
  and and_11 (and_11_out, l_a_shift_left_5_out_4, in_2[3]);
  and and_12 (and_12_out, l_a_shift_left_4_out_4, in_2[4]);
  and and_13 (and_13_out, l_a_shift_left_3_out_4, in_2[5]);
  and and_14 (and_14_out, l_a_shift_left_2_out_4, in_2[6]);
  and and_15 (and_15_out, l_a_shift_left_1_out_4, in_2[7]);
  Adder_part adder_7 (.a(adder_6_out), .b(and_1_out), .out(out_3), .cout(adder_7_cout));  // open: cin
  or or_1 (out_4, adder_7_cout, adder_6_cout, adder_5_cout, adder_4_cout, adder_3_cout, adder_2_cout, adder_1_cout, and_9_out, and_10_out, and_11_out, and_12_out, and_13_out, and_14_out, and_15_out);
endmodule

module MUX_2 (
  input  in_1,
  input  in_2,
  input  in_3,
  output out_4
);

  wire and_1_out, and_2_out, not_1_out;

  not not_1 (not_1_out, in_3);
  and and_1 (and_1_out, in_1, not_1_out);
  and and_2 (and_2_out, in_2, in_3);
  or or_1 (out_4, and_1_out, and_2_out);
endmodule

module MUX_4 (
  input  in_1,
  input  in_2,
  input  in_3,
  input  in_4,
  input  in_5,
  input  in_6,
  output out_7
);

  wire mux_2_1_out_4, mux_2_2_out_4;

  MUX_2 mux_2_1 (.in_1(in_1), .in_2(in_2), .out_4(mux_2_1_out_4), .in_3(in_5));
  MUX_2 mux_2_2 (.in_1(in_3), .in_2(in_4), .out_4(mux_2_2_out_4), .in_3(in_5));
  MUX_2 mux_2_3 (.in_1(mux_2_1_out_4), .in_2(mux_2_2_out_4), .out_4(out_7), .in_3(in_6));
endmodule

module RS_trigger (
  input  in_1,
  input  in_2,
  output Q1,
  output out_4
);

  nor nor_1 (Q1, in_1, out_4);
  nor nor_2 (out_4, in_2, Q1);

  // Notes on the sheet:
  //   R
  //   S
  //   Q
endmodule

module D_trigger (
  input  F,
  input  D,
  output out_3,
  output out_4
);

  wire and_1_out, and_2_out, not_1_out;

  not not_1 (not_1_out, D);
  and and_1 (and_1_out, F, not_1_out);
  and and_2 (and_2_out, F, D);
  RS_trigger rs_trigger_1 (.in_1(and_1_out), .in_2(and_2_out), .Q1(out_3), .out_4(out_4));
endmodule

module D_flip_flop (
  input  in_1,
  input  in_2,
  output out_3
);

  wire d_trigger_1_out_3, not_1_out;

  not not_1 (not_1_out, in_1);
  D_trigger d_trigger_1 (.out_3(d_trigger_1_out_3), .F(not_1_out), .D(in_2));  // open: out_4
  D_trigger d_trigger_2 (.out_3(out_3), .F(in_1), .D(d_trigger_1_out_3));  // open: out_4
endmodule

module Registor (
  input  Lock,
  input  Save,
  input  [7:0] in_3,
  output [7:0] out_4
);

  wire and_1_out;

  and and_1 (and_1_out, Lock, Save);
  D_flip_flop d_flip_flop_1 (.in_1(and_1_out), .in_2(in_3[0]), .out_3(out_4[0]));
  D_flip_flop d_flip_flop_2 (.in_1(and_1_out), .in_2(in_3[1]), .out_3(out_4[1]));
  D_flip_flop d_flip_flop_3 (.in_1(and_1_out), .in_2(in_3[2]), .out_3(out_4[2]));
  D_flip_flop d_flip_flop_4 (.in_1(and_1_out), .in_2(in_3[3]), .out_3(out_4[3]));
  D_flip_flop d_flip_flop_5 (.in_1(and_1_out), .in_2(in_3[4]), .out_3(out_4[4]));
  D_flip_flop d_flip_flop_6 (.in_1(and_1_out), .in_2(in_3[5]), .out_3(out_4[5]));
  D_flip_flop d_flip_flop_7 (.in_1(and_1_out), .in_2(in_3[6]), .out_3(out_4[6]));
  D_flip_flop d_flip_flop_8 (.in_1(and_1_out), .in_2(in_3[7]), .out_3(out_4[7]));
endmodule

module T_counter (
  input  Reset,
  input  [7:0] in_2,
  output [7:0] out_3
);

  wire adder_1_cout, and_1_out, clock_1_out, not_1_out, not_2_out, or_1_out;
  wire [7:0] adder_1_out, transistor_1_out;

  or or_1 (or_1_out, Reset, not_1_out);
  not not_1 (not_1_out, adder_1_cout);
  not not_2 (not_2_out, Reset);
  Transistor #(.width(8)) transistor_1 (.in(adder_1_out), .out(transistor_1_out), .gate(Reset));
  Transistor #(.width(8)) transistor_2 (.in(in_2), .out(transistor_1_out), .gate(not_2_out));
  Clock clock_1 (.out(clock_1_out));
  and and_1 (and_1_out, clock_1_out, or_1_out);
  Register register_1 (.D(transistor_1_out), .Q(out_3), .clk(and_1_out));  // open: en, clr
  Adder_part adder_1 (.a(8'h1), .b(out_3), .out(adder_1_out), .cout(adder_1_cout));  // open: cin
endmodule

module Mem_to_Reg (
  input  [15:0] in_1,
  input  [15:0] in_2,
  output [15:0] out_3,
  output [15:0] out_4,
  output [15:0] out_5,
  output [15:0] out_6
);

  Demultiplexer #(.select(2), .width(16), .enable("false")) demultiplexer_1 (
    .out0(out_3), .out1(out_4), .out2(out_5), .out3(out_6), .in(in_1), .sel(in_2[1:0]));

  // Notes on the sheet:
  //   REG
  //   VAL
endmodule

module Reg_to_Mem (
  input  [15:0] in_1,
  input  [15:0] in_2,
  input  [15:0] in_3,
  input  [15:0] in_4,
  input  [15:0] in_5,
  output [15:0] out_6
);

  Multiplexer #(.select(2), .width(16), .enable("false")) multiplexer_1 (
    .in0(in_1), .in1(in_2), .in2(in_3), .in3(in_4), .out(out_6), .sel(in_5[1:0]));
endmodule

module Reg_to_Reg (
  input  [15:0] in_1,
  input  [15:0] in_2,
  input  [15:0] in_3,
  input  [15:0] in_4,
  input  [15:0] in_5,
  input  [15:0] in_6,
  output [15:0] out_7,
  output [15:0] out_8,
  output [15:0] out_9,
  output [15:0] out_10
);

  wire [15:0] multiplexer_1_out;

  Multiplexer #(.select(2), .width(16), .enable("false")) multiplexer_1 (
    .in0(in_1), .in1(in_2), .in2(in_3), .in3(in_4), .out(multiplexer_1_out), .sel(in_5[1:0]));
  Demultiplexer #(.select(2), .width(16), .enable("false")) demultiplexer_1 (
    .out0(out_7), .out1(out_8), .out2(out_9), .out3(out_10), .in(multiplexer_1_out), .sel(in_6[1:0]));
endmodule
